# Fritzing sketch sketch (saved by Fritzing 1.0.1rc)

parts:
  M4 = DOIT Esp32 DevKit v1 (30 pins long, 11 pins width) [part_number=ESP32S-PIN30]
  U1 = WS2812 RGB LED strip
  Part2 = Mono 0.96in 128x64 OLED with STEMMA QT
  Power_plug1 = Power plug

nets:
  3V3: M4.3V3, Part2.VCC
  GND: M4.GND, U1.GND, Part2.GND, Power_plug1.GND
  N1: M4.D2, U1.DIN
  N2: M4.D21, Part2.SDA
  N3: M4.D22, Part2.SCL
  VCC: M4.VIN, U1.VCC, Power_plug1.VCC

custom parts:
  DOIT Esp32 DevKit v1 (30 pins long, 11 pins width): The DOIT Esp32 DevKit v1 is one of the development board created by DOIT to evaluate the ESP-WROOM-32 module. It is based on the ESP32 microcontroller that boasts Wifi, Bluetooth, Ethernet and Low Power support all in a single chip. (vanepp) made breadboard work, adjusted pin numbering and labels and reduced size of schematic and cleaned up pcb. This chip is 30pins long (2 x15) and 11 pins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
  WS2812 RGB LED strip: WS2812 strip
  Mono 0.96in 128x64 OLED with STEMMA QT: These displays are small, only about 1" diagonal, but very readable due to the high contrast of an OLED display. This display is made of 128x64 individual white OLED pixels, each one is turned on or off by the controller chip. Because the display makes its own light, no backlight is required. This reduces the power required to run the OLED and is why the display has such high contrast; we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
